// Logisim project hw3.circ as structural Verilog: 2 circuits, main circuit fullAdder
module fullAdder (
  input  inA,
  input  inB,
  input  carryIn,
  output sum,
  output carryOut
);
endmodule

module TOP_add4bit (
  input  [3:0] A,
  input  [3:0] B,
  input  carryIn,
  output [3:0] sum,
  output carryOut
);


  // Other names for the same wires on the sheet: cin = carryIn; cout = carryOut; s0 = sum[0]; s1 = sum[1];
  //   s2 = sum[2]; s3 = sum[3]
endmodule
