// Logisim project hw4.circ as structural Verilog: 1 circuit, main circuit pattern
// PS1
module pattern (
  input  x,
  input  reset,
  output z
);

  wire and_1_out, and_2_out, and_3_out, and_4_out, and_5_out, clock_1_out, not_1_out, not_2_out, not_3_out,
       not_4_out, not_5_out, not_6_out, NS0, NS1, PS0, PS1;

  Clock clock_1 (.out(clock_1_out));
  not not_1 (not_1_out, PS0);
  not not_2 (not_2_out, PS1);
  and and_1 (and_1_out, PS1, not_1_out);
  and and_2 (and_2_out, not_2_out, PS0, x);
  or or_1 (NS1, and_1_out, and_2_out);
  Register #(.width(2)) register_1 (.D({NS1, NS0}), .Q({PS1, PS0}), .clk(clock_1_out), .clr(reset));  // open: en
  not not_3 (not_3_out, PS0);
  not not_4 (not_4_out, x);
  not not_5 (not_5_out, PS1);
  not not_6 (not_6_out, PS0);
  and and_3 (and_3_out, PS1, not_3_out, not_4_out);
  and and_4 (and_4_out, not_5_out, not_6_out, x);
  and and_5 (and_5_out, PS1, PS0, x);
  or or_2 (NS0, and_3_out, and_4_out, and_5_out);
  and and_6 (z, PS1, PS0, x);
endmodule
