// Logisim project hw5_patternD.circ as structural Verilog: 2 circuits, main circuit TOP_patternD
module TOP_patternD (
  input  x,
  input  reset,
  input  clk,
  output z,
  output [2:0] curState
);

  wire [2:0] ns, psInv;

  state_comb state_comb_1 (.ps(curState), .x(x), .ns(ns), .z(z), .psInv(psInv));
  D_Flip_Flop s2 (.clk(clk), .D(ns[2]), .Q(curState[2]), .Qn(psInv[2]), .reset(reset));  // open: preset, en
  D_Flip_Flop s1 (.clk(clk), .D(ns[1]), .Q(curState[1]), .Qn(psInv[1]), .reset(reset));  // open: preset, en
  D_Flip_Flop s0 (.clk(clk), .D(ns[0]), .Q(curState[0]), .Qn(psInv[0]), .reset(reset));  // open: preset, en

  // Other names for the same wires on the sheet: ps[2:0] = curState; s0 = curState[0]; s1 = curState[1];
  //   s2 = curState[2]; s0_prime = psInv[0]; s1_prime = psInv[1]; s2_prime = psInv[2]; rst = reset
endmodule

module state_comb (
  input  [2:0] ps,
  input  [2:0] psInv,
  input  x,
  output [2:0] ns,
  output z
);

  wire and_1_out, and_2_out, and_3_out, and_4_out, and_5_out, and_6_out, x_prime;

  not not_1 (x_prime, x);
  and and_1 (and_1_out, ps[2], psInv[0], x_prime);
  or or_1 (ns[2], ps[1], and_1_out);
  and and_2 (and_2_out, psInv[1], x_prime);
  and and_3 (and_3_out, psInv[2], psInv[1], psInv[0], x);
  and and_4 (and_4_out, ps[2], ps[1]);
  and and_5 (and_5_out, ps[1], psInv[0], x);
  and and_6 (and_6_out, ps[2], ps[0], x);
  or or_2 (ns[0], and_2_out, and_3_out);
  or or_3 (z, and_4_out, and_5_out, and_6_out);

  assign ns[1] = x;

  // Other names for the same wires on the sheet: ns1 = x; s0 = ps[0]; s1 = ps[1]; s2 = ps[2]; s0_prime = psInv[0];
  //   s1_prime = psInv[1]; s2_prime = psInv[2]
endmodule
