// Logisim project hw5_patternJK.circ as structural Verilog: 2 circuits, main circuit TOP_patternJK
module TOP_patternJK (
  input  x,
  input  reset,
  input  clk,
  output z,
  output [2:0] curState
);

  wire [2:0] nj, nk, psInv;

  state_comb state_comb_1 (.ps(curState), .x(x), .nj(nj), .z(z), .psInv(psInv), .nk(nk));
  J_K_Flip_Flop s2 (
    .J(nj[2]), .clk(clk), .K(nk[2]), .Q(curState[2]), .Qn(psInv[2]), .reset(reset));  // open: preset, en
  J_K_Flip_Flop s1 (
    .J(nj[1]), .clk(clk), .K(nk[1]), .Q(curState[1]), .Qn(psInv[1]), .reset(reset));  // open: preset, en
  J_K_Flip_Flop s0 (
    .J(nj[0]), .clk(clk), .K(nk[0]), .Q(curState[0]), .Qn(psInv[0]), .reset(reset));  // open: preset, en

  // Other names for the same wires on the sheet: ps[2:0] = curState; s0 = curState[0]; s1 = curState[1];
  //   s2 = curState[2]; s0_prime = psInv[0]; s1_prime = psInv[1]; s2_prime = psInv[2]; rst = reset
endmodule

module state_comb (
  input  [2:0] ps,
  input  [2:0] psInv,
  input  x,
  output [2:0] nj,
  output [2:0] nk,
  output z
);

  wire and_1_out, and_2_out, and_3_out, and_4_out, and_5_out, and_6_out;

  not not_1 (nk[1], x);
  and and_1 (and_1_out, psInv[1], nk[1]);
  and and_2 (and_2_out, psInv[2], psInv[1], x);
  or or_1 (nj[0], and_1_out, and_2_out);
  and and_3 (and_3_out, psInv[1], x);
  or or_2 (nk[0], ps[1], x);
  or or_3 (nk[2], ps[0], and_3_out);
  and and_4 (and_4_out, ps[2], ps[1]);
  and and_5 (and_5_out, ps[1], psInv[0], x);
  and and_6 (and_6_out, ps[2], ps[0], x);
  or or_4 (z, and_4_out, and_5_out, and_6_out);

  assign nj[2:1] = {ps[1], x};

  // Other names for the same wires on the sheet: j0 = nj[0]; j1 = x; j2 = ps[1]; s1 = ps[1]; k0 = nk[0]; k1 = nk[1];
  //   x_prime = nk[1]; k2 = nk[2]; s0 = ps[0]; s2 = ps[2]; s0_prime = psInv[0]; s1_prime = psInv[1];
  //   s2_prime = psInv[2]
endmodule
